# Fritzing sketch PulseSensor_BlinkLed (saved by Fritzing 0.9.2b)
breadboards: 1

parts:
  元件1 = Arduino Pro Mini v13
  RGB_LED = RGB LED (com. cathode, rgb) [package="5 mm [THT]"]

nets:
  N1: 元件1.GND, RGB_LED.common_cathode
  N2: 元件1.D9_PWM, RGB_LED.green_anode
  N3: 元件1.D6_PWM, RGB_LED.blue_anode
  N4: 元件1.D5_PWM, RGB_LED.red_anode
